# Fritzing sketch DH11-SSD1306 (saved by Fritzing 0.9.3b)
breadboards: 1

parts:
  o1 = Module display OLED I2C 128x64 SSD1306 [package=THT]
  DHT1 = DHT11 Humitidy and Temperature Sensor
  Part1 = Arduino Uno (Rev3)

nets:
  GND: o1.GND, DHT1.GND, Part1.D2, Part1.GND
  VCC: o1.VCC, DHT1.VDD, Part1.5V
  N1: o1.SCL, Part1.A5/SCL

custom parts:
  Module display OLED I2C 128x64 SSD1306: Ecran OLED I2C SSD163 de 128x64 avec connexion I2C
  DHT11 Humitidy and Temperature Sensor: DHT11 Humidity and Temperature Sensor
